// Logisim project LabArqui.circ as structural Verilog: 14 circuits, main circuit main
module main (
  input  [7:0] in_1,
  input  [7:0] in_2,
  input  [7:0] in_3,
  input  [7:0] in_4,
  input  [7:0] in_5,
  input  [7:0] in_6,
  input  [7:0] in_7,
  input  [7:0] in_8,
  output [7:0] out_9,
  output [7:0] out_10,
  output [7:0] out_11,
  output [7:0] out_12,
  output [7:0] out_13,
  output [7:0] out_14,
  output [7:0] out_15,
  output [7:0] out_16
);

  // Probe on in_1
  // Probe on in_5
  // Probe on in_2
  // Probe on in_3
  // Probe on in_4
  // Probe on in_6
  // Probe on in_7
  // Probe on in_8
  EightSwitcher eightswitcher_1 (
    .in_1(in_1), .in_2(in_2), .in_3(in_3), .in_4(in_4), .in_5(in_5), .in_6(in_6), .in_7(in_7), .in_8(in_8),
    .out_9(out_9), .out_10(out_10), .out_11(out_11), .out_12(out_12), .out_13(out_13), .out_14(out_14),
    .out_15(out_15), .out_16(out_16));
  // Probe on out_9
  // Probe on out_10
  // Probe on out_11
  // Probe on out_12
  // Probe on out_13
  // Probe on out_14
  // Probe on out_15
  // Probe on out_16
endmodule

module OneBitComparator (
  input  A,
  input  B,
  output AGB,
  output ALB,
  output AEB
);

  wire not_1_out, not_2_out, or_1_out;

  not not_1 (not_1_out, B);
  not not_2 (not_2_out, A);
  and and_1 (AGB, A, not_1_out);
  and and_2 (ALB, not_2_out, B);
  or or_1 (or_1_out, ALB, AGB);
  not not_3 (AEB, or_1_out);

  // Notes on the sheet:
  //   A>B
  //   A<B
  //   A=B
endmodule

module EightBitComparator (
  input  A7,
  input  B7,
  input  A6,
  input  A5,
  input  A4,
  input  A3,
  input  A2,
  input  A1,
  input  A0,
  input  B6,
  input  B5,
  input  B4,
  input  B3,
  input  B2,
  input  B1,
  input  B0,
  output AGB,
  output ALB,
  output AEB
);

  wire comparatorgluer_1_aeb, comparatorgluer_1_agb, comparatorgluer_1_alb, fourbitcomparator_1_aeb,
       fourbitcomparator_1_agb, fourbitcomparator_1_alb, not_1_out, onebitcomparator_1_aeb,
       onebitcomparator_1_agb, onebitcomparator_1_alb, ourxor_1_out_3, twobitcomparator_1_aeb,
       twobitcomparator_1_agb, twobitcomparator_1_alb;
  wire [2:0] comparatorgluer_2_agb, onebitcomparator_2_agb;

  OurXOR ourxor_1 (.in_1(A7), .in_2(B7), .out_3(ourxor_1_out_3));
  FourBitComparator fourbitcomparator_1 (
    .A3(A6), .A2(A5), .A1(A4), .A0(A3), .B3(B6), .B2(B5), .B1(B4), .B0(B3), .AGB(fourbitcomparator_1_agb),
    .ALB(fourbitcomparator_1_alb), .AEB(fourbitcomparator_1_aeb));
  TwoBitComparator twobitcomparator_1 (
    .A1(A2), .A0(A1), .B1(B2), .B0(B1), .AGB(twobitcomparator_1_agb), .ALB(twobitcomparator_1_alb),
    .AEB(twobitcomparator_1_aeb));
  OneBitComparator onebitcomparator_1 (
    .A(A0), .B(B0), .AGB(onebitcomparator_1_agb), .ALB(onebitcomparator_1_alb), .AEB(onebitcomparator_1_aeb));
  OneBitComparator onebitcomparator_2 (
    .A(B7), .B(A7), .AGB(onebitcomparator_2_agb[0]), .ALB(onebitcomparator_2_agb[1]),
    .AEB(onebitcomparator_2_agb[2]));
  ComparatorGluer comparatorgluer_1 (
    .PSBG(fourbitcomparator_1_agb), .PSBL(fourbitcomparator_1_alb), .PSBE(fourbitcomparator_1_aeb),
    .LSBG(twobitcomparator_1_agb), .LSBL(twobitcomparator_1_alb), .LSBE(twobitcomparator_1_aeb),
    .AGB(comparatorgluer_1_agb), .ALB(comparatorgluer_1_alb), .AEB(comparatorgluer_1_aeb));
  not not_1 (not_1_out, ourxor_1_out_3);
  ComparatorGluer comparatorgluer_2 (
    .PSBG(comparatorgluer_1_agb), .PSBL(comparatorgluer_1_alb), .PSBE(comparatorgluer_1_aeb),
    .LSBG(onebitcomparator_1_agb), .LSBL(onebitcomparator_1_alb), .LSBE(onebitcomparator_1_aeb),
    .AGB(comparatorgluer_2_agb[0]), .ALB(comparatorgluer_2_agb[1]), .AEB(comparatorgluer_2_agb[2]));
  Our31MUX our31mux_1 (.CH1(comparatorgluer_2_agb), .S(not_1_out), .CH0(onebitcomparator_2_agb), .G({AEB, ALB, AGB}));
endmodule

module TwoBitComparator (
  input  A1,
  input  A0,
  input  B1,
  input  B0,
  output AGB,
  output ALB,
  output AEB
);

  wire onebitcomparator_1_aeb, onebitcomparator_1_agb, onebitcomparator_1_alb, onebitcomparator_2_aeb,
       onebitcomparator_2_agb, onebitcomparator_2_alb;

  OneBitComparator onebitcomparator_1 (
    .A(A1), .B(B1), .AGB(onebitcomparator_1_agb), .ALB(onebitcomparator_1_alb), .AEB(onebitcomparator_1_aeb));
  OneBitComparator onebitcomparator_2 (
    .A(A0), .B(B0), .AGB(onebitcomparator_2_agb), .ALB(onebitcomparator_2_alb), .AEB(onebitcomparator_2_aeb));
  ComparatorGluer comparatorgluer_1 (
    .PSBG(onebitcomparator_1_agb), .PSBL(onebitcomparator_1_alb), .PSBE(onebitcomparator_1_aeb),
    .LSBG(onebitcomparator_2_agb), .LSBL(onebitcomparator_2_alb), .LSBE(onebitcomparator_2_aeb), .AGB(AGB),
    .ALB(ALB), .AEB(AEB));

  // Notes on the sheet:
  //   +SBIT
  //   -SBIT
endmodule

module FourBitComparator (
  input  A3,
  input  A2,
  input  A1,
  input  A0,
  input  B3,
  input  B2,
  input  B1,
  input  B0,
  output AGB,
  output ALB,
  output AEB
);

  wire twobitcomparator_1_aeb, twobitcomparator_1_agb, twobitcomparator_1_alb, twobitcomparator_2_aeb,
       twobitcomparator_2_agb, twobitcomparator_2_alb;

  TwoBitComparator twobitcomparator_1 (
    .A1(A3), .A0(A2), .B1(B3), .B0(B2), .AGB(twobitcomparator_1_agb), .ALB(twobitcomparator_1_alb),
    .AEB(twobitcomparator_1_aeb));
  TwoBitComparator twobitcomparator_2 (
    .A1(A1), .A0(A0), .B1(B1), .B0(B0), .AGB(twobitcomparator_2_agb), .ALB(twobitcomparator_2_alb),
    .AEB(twobitcomparator_2_aeb));
  ComparatorGluer comparatorgluer_1 (
    .PSBG(twobitcomparator_1_agb), .PSBL(twobitcomparator_1_alb), .PSBE(twobitcomparator_1_aeb),
    .LSBG(twobitcomparator_2_agb), .LSBL(twobitcomparator_2_alb), .LSBE(twobitcomparator_2_aeb), .AGB(AGB),
    .ALB(ALB), .AEB(AEB));

  // Notes on the sheet:
  //   +SBIT
  //   -SBIT
endmodule

module OurXOR (
  input  in_1,
  input  in_2,
  output out_3
);

  wire and_1_out, and_2_out;

  and and_1 (and_1_out, in_1, ~in_2);  // AND_Gate
  and and_2 (and_2_out, ~in_1, in_2);  // AND_Gate
  or or_1 (out_3, and_1_out, and_2_out);
endmodule

module Switcher (
  input  [7:0] A,
  input  [7:0] B,
  output [7:0] G,
  output [7:0] L
);

  wire eightbitcomparator_1_agb;

  // Probe on A
  // Probe on B
  // Probe on G
  Our81MUX our81mux_1 (.S(eightbitcomparator_1_agb), .CH0(B), .CH1(A), .O(G));
  Our81MUX our81mux_2 (.S(eightbitcomparator_1_agb), .CH0(A), .CH1(B), .O(L));
  // Probe on L
  EightBitComparator eightbitcomparator_1 (
    .B3(B[3]), .B5(B[5]), .A0(A[0]), .A2(A[2]), .A4(A[4]), .A6(A[6]), .A7(A[7]), .B7(B[7]), .A5(A[5]),
    .A3(A[3]), .A1(A[1]), .B6(B[6]), .B4(B[4]), .B2(B[2]), .B1(B[1]), .B0(B[0]),
    .AGB(eightbitcomparator_1_agb));  // open: ALB, AEB

  // Notes on the sheet:
  //   +
  //   -
endmodule

module FourSwitcher (
  input  [7:0] in_1,
  input  [7:0] in_2,
  input  [7:0] in_3,
  input  [7:0] in_4,
  output [7:0] GG,
  output [7:0] GL,
  output [7:0] LG,
  output [7:0] LL
);

  wire [7:0] switcher_1_g, switcher_1_l, switcher_2_g, switcher_2_l, switcher_3_l, switcher_4_g;

  // Probe on in_1
  // Probe on in_2
  // Probe on in_3
  // Probe on in_4
  Switcher switcher_1 (.A(in_1), .B(in_2), .G(switcher_1_g), .L(switcher_1_l));
  Switcher switcher_2 (.A(in_3), .B(in_4), .G(switcher_2_g), .L(switcher_2_l));
  Switcher switcher_3 (.A(switcher_1_g), .B(switcher_2_g), .G(GG), .L(switcher_3_l));
  Switcher switcher_4 (.A(switcher_1_l), .B(switcher_2_l), .G(switcher_4_g), .L(LL));
  Switcher switcher_5 (.A(switcher_3_l), .B(switcher_4_g), .G(GL), .L(LG));
  // Probe on GG
  // Probe on GL
  // Probe on LG
  // Probe on LL
endmodule

module Our21MUX (
  input  CH0,
  input  CH1,
  input  S,
  output O
);

  wire and_1_out, and_2_out, not_1_out;

  not not_1 (not_1_out, S);
  and and_1 (and_1_out, CH0, not_1_out);
  and and_2 (and_2_out, CH1, S);
  or or_1 (O, and_1_out, and_2_out);
endmodule

module Our31MUX (
  input  S,
  input  [2:0] CH0,
  input  [2:0] CH1,
  output [2:0] G
);

  Our21MUX our21mux_1 (.S(S), .CH0(CH0[0]), .CH1(CH1[0]), .O(G[0]));
  Our21MUX our21mux_2 (.S(S), .CH0(CH0[1]), .CH1(CH1[1]), .O(G[1]));
  Our21MUX our21mux_3 (.S(S), .CH0(CH0[2]), .CH1(CH1[2]), .O(G[2]));
endmodule

module Our41MUX (
  input  S,
  input  [3:0] CH0,
  input  [3:0] CH1,
  output [3:0] O
);

  Our21MUX our21mux_1 (.S(S), .CH0(CH0[0]), .CH1(CH1[0]), .O(O[0]));
  Our21MUX our21mux_2 (.S(S), .CH0(CH0[1]), .CH1(CH1[1]), .O(O[1]));
  Our21MUX our21mux_3 (.S(S), .CH0(CH0[2]), .CH1(CH1[2]), .O(O[2]));
  Our21MUX our21mux_4 (.S(S), .CH0(CH0[3]), .CH1(CH1[3]), .O(O[3]));
endmodule

module Our81MUX (
  input  S,
  input  [7:0] CH0,
  input  [7:0] CH1,
  output [7:0] O
);

  Our41MUX our41mux_1 (.S(S), .CH0(CH0[3:0]), .CH1(CH1[3:0]), .O(O[3:0]));
  Our41MUX our41mux_2 (.S(S), .CH0(CH0[7:4]), .CH1(CH1[7:4]), .O(O[7:4]));
endmodule

module EightSwitcher (
  input  [7:0] in_1,
  input  [7:0] in_2,
  input  [7:0] in_3,
  input  [7:0] in_4,
  input  [7:0] in_5,
  input  [7:0] in_6,
  input  [7:0] in_7,
  input  [7:0] in_8,
  output [7:0] out_9,
  output [7:0] out_10,
  output [7:0] out_11,
  output [7:0] out_12,
  output [7:0] out_13,
  output [7:0] out_14,
  output [7:0] out_15,
  output [7:0] out_16
);

  wire [7:0] fourswitcher_1_gg, fourswitcher_1_gl, fourswitcher_1_lg, fourswitcher_1_ll, fourswitcher_2_gg,
       fourswitcher_2_gl, fourswitcher_2_lg, fourswitcher_2_ll, fourswitcher_3_lg, fourswitcher_3_ll,
       fourswitcher_4_gg, fourswitcher_4_gl;

  // Probe on in_1
  // Probe on in_5
  // Probe on in_2
  // Probe on in_3
  // Probe on in_6
  // Probe on in_7
  // Probe on in_4
  // Probe on in_8
  FourSwitcher fourswitcher_1 (
    .in_1(in_1), .in_2(in_2), .in_3(in_3), .in_4(in_4), .GG(fourswitcher_1_gg), .GL(fourswitcher_1_gl),
    .LG(fourswitcher_1_lg), .LL(fourswitcher_1_ll));
  FourSwitcher fourswitcher_2 (
    .in_1(in_5), .in_2(in_6), .in_3(in_7), .in_4(in_8), .GG(fourswitcher_2_gg), .GL(fourswitcher_2_gl),
    .LG(fourswitcher_2_lg), .LL(fourswitcher_2_ll));
  FourSwitcher fourswitcher_3 (
    .in_1(fourswitcher_1_gg), .in_2(fourswitcher_1_gl), .in_3(fourswitcher_2_gg), .in_4(fourswitcher_2_gl),
    .GG(out_9), .GL(out_10), .LG(fourswitcher_3_lg), .LL(fourswitcher_3_ll));
  FourSwitcher fourswitcher_4 (
    .in_1(fourswitcher_1_lg), .in_2(fourswitcher_1_ll), .in_3(fourswitcher_2_lg), .in_4(fourswitcher_2_ll),
    .GG(fourswitcher_4_gg), .GL(fourswitcher_4_gl), .LG(out_15), .LL(out_16));
  // Probe on out_9
  // Probe on out_10
  // Probe on out_11
  FourSwitcher fourswitcher_5 (
    .in_1(fourswitcher_3_lg), .in_2(fourswitcher_3_ll), .in_3(fourswitcher_4_gg), .in_4(fourswitcher_4_gl),
    .GG(out_11), .GL(out_12), .LG(out_13), .LL(out_14));
  // Probe on out_13
  // Probe on out_14
  // Probe on out_15
  // Probe on out_16
  // Probe on out_12
endmodule

module ComparatorGluer (
  input  PSBG,
  input  PSBL,
  input  PSBE,
  input  LSBG,
  input  LSBL,
  input  LSBE,
  output AGB,
  output ALB,
  output AEB
);

  wire and_1_out, and_2_out, not_1_out, not_2_out;

  not not_1 (not_1_out, PSBL);
  not not_2 (not_2_out, PSBG);
  and and_1 (and_1_out, not_1_out, LSBG);
  and and_2 (and_2_out, LSBL, not_2_out);
  or or_1 (AGB, PSBG, and_1_out);
  or or_2 (ALB, PSBL, and_2_out);
  and and_3 (AEB, PSBE, LSBE);
endmodule
