// Logisim project LabArqui2.circ as structural Verilog: 8 circuits, main circuit main
module main (
  input  in_1,
  output [3:0] out_2
);

  wire bts_1_s1, bts_1_s2, bts_1_s3, clock_1_out, random_1_out, ss_1_a, ss_1_b, ss_1_c, ss_1_d, ss_1_e,
       ss_1_f, ss_1_g, ss_2_a, ss_2_b, ss_2_c, ss_2_d, ss_2_e, ss_2_f, ss_2_g, ss_3_a, ss_3_b, ss_3_c,
       ss_3_d, ss_3_e, ss_3_f, ss_3_g, ss_4_a, ss_4_b, ss_4_c, ss_4_d, ss_4_e, ss_4_f, ss_4_g, ss_5_a,
       ss_5_b, ss_5_c, ss_5_d, ss_5_e, ss_5_f, ss_5_g, ss_6_a, ss_6_b, ss_6_c, ss_6_d, ss_6_e, ss_6_f,
       ss_6_g, ss_7_a, ss_7_b, ss_7_c, ss_7_d, ss_7_e, ss_7_f, ss_7_g, ss_8_a, ss_8_b, ss_8_c, ss_8_d,
       ss_8_e, ss_8_f, ss_8_g, ss_9_a, ss_9_b, ss_9_c, ss_9_d, ss_9_e, ss_9_f, ss_9_g;
  wire [3:0] ocplusc2d_1_s1ss0, ocplusc2d_1_s1ss1, ocplusc2d_1_s1ss2, ocplusc2d_1_s2ss0, ocplusc2d_1_s2ss1,
       ocplusc2d_1_s2ss2, ocplusc2d_1_s3ss0, ocplusc2d_1_s3ss1, ocplusc2d_1_s3ss2;

  Clock clock_1 (.out(clock_1_out));
  Random #(.width(1)) random_1 (.clr(in_1), .clk(clock_1_out), .out(random_1_out));  // open: next
  BTS bts_1 (
    .X(random_1_out), .CLK(clock_1_out), .RESET(in_1), .S1(bts_1_s1), .S2(bts_1_s2), .S3(bts_1_s3),
    .STATE(out_2));
  OCPLUSC2D ocplusc2d_1 (
    .S1(bts_1_s1), .S2(bts_1_s2), .S3(bts_1_s3), .CLK(clock_1_out), .R(in_1), .S1SS2(ocplusc2d_1_s1ss2),
    .S1SS1(ocplusc2d_1_s1ss1), .S1SS0(ocplusc2d_1_s1ss0), .S2SS2(ocplusc2d_1_s2ss2),
    .S2SS1(ocplusc2d_1_s2ss1), .S2SS0(ocplusc2d_1_s2ss0), .S3SS2(ocplusc2d_1_s3ss2),
    .S3SS1(ocplusc2d_1_s3ss1), .S3SS0(ocplusc2d_1_s3ss0));
  _7_Segment_Display u_7_segment_display_1 (
    .g(ss_1_g), .f(ss_1_f), .a(ss_1_a), .b(ss_1_b), .e(ss_1_e), .d(ss_1_d), .c(ss_1_c));  // open: dp
  _7_Segment_Display u_7_segment_display_2 (
    .g(ss_2_g), .f(ss_2_f), .a(ss_2_a), .b(ss_2_b), .e(ss_2_e), .d(ss_2_d), .c(ss_2_c));  // open: dp
  SS ss_1 (
    .in_1(ocplusc2d_1_s1ss2), .A(ss_1_a), .B(ss_1_b), .C(ss_1_c), .D(ss_1_d), .E(ss_1_e), .F(ss_1_f),
    .G(ss_1_g));
  SS ss_2 (
    .in_1(ocplusc2d_1_s2ss2), .A(ss_2_a), .B(ss_2_b), .C(ss_2_c), .D(ss_2_d), .E(ss_2_e), .F(ss_2_f),
    .G(ss_2_g));
  SS ss_3 (
    .in_1(ocplusc2d_1_s3ss2), .A(ss_3_a), .B(ss_3_b), .C(ss_3_c), .D(ss_3_d), .E(ss_3_e), .F(ss_3_f),
    .G(ss_3_g));
  _7_Segment_Display u_7_segment_display_3 (
    .g(ss_3_g), .f(ss_3_f), .a(ss_3_a), .b(ss_3_b), .e(ss_3_e), .d(ss_3_d), .c(ss_3_c));  // open: dp
  _7_Segment_Display u_7_segment_display_4 (
    .g(ss_4_g), .f(ss_4_f), .a(ss_4_a), .b(ss_4_b), .e(ss_4_e), .d(ss_4_d), .c(ss_4_c));  // open: dp
  _7_Segment_Display u_7_segment_display_5 (
    .g(ss_5_g), .f(ss_5_f), .a(ss_5_a), .b(ss_5_b), .e(ss_5_e), .d(ss_5_d), .c(ss_5_c));  // open: dp
  SS ss_4 (
    .in_1(ocplusc2d_1_s1ss1), .A(ss_4_a), .B(ss_4_b), .C(ss_4_c), .D(ss_4_d), .E(ss_4_e), .F(ss_4_f),
    .G(ss_4_g));
  SS ss_5 (
    .in_1(ocplusc2d_1_s2ss1), .A(ss_5_a), .B(ss_5_b), .C(ss_5_c), .D(ss_5_d), .E(ss_5_e), .F(ss_5_f),
    .G(ss_5_g));
  _7_Segment_Display u_7_segment_display_6 (
    .g(ss_6_g), .f(ss_6_f), .a(ss_6_a), .b(ss_6_b), .e(ss_6_e), .d(ss_6_d), .c(ss_6_c));  // open: dp
  _7_Segment_Display u_7_segment_display_7 (
    .g(ss_7_g), .f(ss_7_f), .a(ss_7_a), .b(ss_7_b), .e(ss_7_e), .d(ss_7_d), .c(ss_7_c));  // open: dp
  _7_Segment_Display u_7_segment_display_8 (
    .g(ss_8_g), .f(ss_8_f), .a(ss_8_a), .b(ss_8_b), .e(ss_8_e), .d(ss_8_d), .c(ss_8_c));  // open: dp
  SS ss_6 (
    .in_1(ocplusc2d_1_s3ss1), .A(ss_6_a), .B(ss_6_b), .C(ss_6_c), .D(ss_6_d), .E(ss_6_e), .F(ss_6_f),
    .G(ss_6_g));
  SS ss_7 (
    .in_1(ocplusc2d_1_s1ss0), .A(ss_7_a), .B(ss_7_b), .C(ss_7_c), .D(ss_7_d), .E(ss_7_e), .F(ss_7_f),
    .G(ss_7_g));
  SS ss_8 (
    .in_1(ocplusc2d_1_s2ss0), .A(ss_8_a), .B(ss_8_b), .C(ss_8_c), .D(ss_8_d), .E(ss_8_e), .F(ss_8_f),
    .G(ss_8_g));
  _7_Segment_Display u_7_segment_display_9 (
    .g(ss_9_g), .f(ss_9_f), .a(ss_9_a), .b(ss_9_b), .e(ss_9_e), .d(ss_9_d), .c(ss_9_c));  // open: dp
  SS ss_9 (
    .in_1(ocplusc2d_1_s3ss0), .A(ss_9_a), .B(ss_9_b), .C(ss_9_c), .D(ss_9_d), .E(ss_9_e), .F(ss_9_f),
    .G(ss_9_g));

  // Notes on the sheet:
  //   111
  //   0110
  //   11011
endmodule

module BTS (
  input  X,
  input  CLK,
  input  RESET,
  output S1,
  output S2,
  output S3,
  output [3:0] STATE
);

  wire statemachine_1_j0, statemachine_1_j1, statemachine_1_j2, statemachine_1_j3, statemachine_1_k0,
       statemachine_1_k1, statemachine_1_k2, statemachine_1_k3;

  StateMachine statemachine_1 (
    .Q3(STATE[3]), .Q2(STATE[2]), .Q1(STATE[1]), .Q0(STATE[0]), .X(X), .J3(statemachine_1_j3),
    .K3(statemachine_1_k3), .J2(statemachine_1_j2), .K2(statemachine_1_k2), .J1(statemachine_1_j1),
    .K1(statemachine_1_k1), .J0(statemachine_1_j0), .K0(statemachine_1_k0));
  J_K_Flip_Flop Q3 (
    .J(statemachine_1_j3), .K(statemachine_1_k3), .clk(CLK), .Q(STATE[3]), .reset(RESET));  // open: Qn, preset
  J_K_Flip_Flop Q2 (
    .J(statemachine_1_j2), .K(statemachine_1_k2), .clk(CLK), .Q(STATE[2]), .reset(RESET));  // open: Qn, preset
  J_K_Flip_Flop Q1 (
    .J(statemachine_1_j1), .K(statemachine_1_k1), .clk(CLK), .Q(STATE[1]), .reset(RESET));  // open: Qn, preset
  J_K_Flip_Flop Q0 (
    .J(statemachine_1_j0), .K(statemachine_1_k0), .clk(CLK), .Q(STATE[0]), .reset(RESET));  // open: Qn, preset
  SMRecognizer smrecognizer_1 (.Q3(STATE[3]), .Q2(STATE[2]), .Q1(STATE[1]), .Q0(STATE[0]), .S1(S1), .S2(S2), .S3(S3));
endmodule

module StateMachine (
  input  Q3,
  input  Q2,
  input  Q1,
  input  Q0,
  input  X,
  output J3,
  output K3,
  output J2,
  output K2,
  output J1,
  output K1,
  output J0,
  output K0
);

  wire and_1_out, and_2_out, and_3_out, and_4_out, and_5_out, and_6_out, and_7_out, and_8_out, and_9_out,
       and_10_out, and_11_out, and_12_out, and_13_out, and_15_out, and_16_out;

  and and_1 (and_1_out, Q2, ~Q1, X);  // AND_Gate
  and and_2 (and_2_out, Q1, ~X);  // AND_Gate
  and and_3 (and_3_out, ~Q2, Q1);  // AND_Gate
  and and_4 (and_4_out, ~Q2, ~X);  // AND_Gate
  and and_5 (and_5_out, Q2, Q1, X);
  and and_6 (and_6_out, ~Q2, ~Q1, X);  // AND_Gate
  and and_7 (and_7_out, X, Q3);
  and and_8 (and_8_out, ~Q3, Q2, Q0);  // AND_Gate
  and and_9 (and_9_out, Q2, ~X);  // AND_Gate
  and and_10 (and_10_out, Q0, X);
  and and_11 (and_11_out, Q0, Q2);
  or or_1 (J0, and_5_out, and_6_out, and_7_out);
  or or_2 (K0, and_1_out, and_2_out, and_3_out, and_4_out);
  or or_3 (K1, and_8_out, and_9_out);
  and and_12 (and_12_out, ~Q0, ~X);  // AND_Gate
  and and_13 (and_13_out, Q0, X);
  and and_14 (K2, ~Q1, Q0, X);  // AND_Gate
  or or_4 (J1, and_10_out, and_11_out);
  or or_5 (K3, Q1, and_12_out, and_13_out);
  and and_15 (and_15_out, Q2, ~Q1, ~Q0, X);  // AND_Gate
  and and_16 (and_16_out, Q2, ~Q1, Q0, ~X);  // AND_Gate
  or or_6 (J3, and_15_out, and_16_out);
  not not_1 (J2, X);
endmodule

module SMRecognizer (
  input  Q3,
  input  Q2,
  input  Q1,
  input  Q0,
  output S1,
  output S2,
  output S3
);

  and and_1 (S1, ~Q3, ~Q2, Q1, ~Q0);  // AND_Gate
  and and_2 (S2, Q3, Q2, Q1, Q0);
  and and_3 (S3, ~Q3, Q2, ~Q1, Q0);  // AND_Gate
endmodule

module OurCounter (
  input  S,
  input  CLK,
  input  R,
  output [7:0] out_4
);

  wire and_1_out, d_ff_1_qn, d_ff_2_qn, d_ff_3_qn, d_ff_4_qn, d_ff_5_qn, d_ff_6_qn, d_ff_7_qn, d_ff_8_qn;

  D_Flip_Flop d_ff_1 (.D(d_ff_1_qn), .clk(and_1_out), .Q(out_4[0]), .Qn(d_ff_1_qn), .reset(R));  // open: preset
  and and_1 (and_1_out, S, ~CLK);  // AND_Gate
  D_Flip_Flop d_ff_2 (.D(d_ff_2_qn), .clk(d_ff_1_qn), .Q(out_4[1]), .Qn(d_ff_2_qn), .reset(R));  // open: preset
  D_Flip_Flop d_ff_3 (.D(d_ff_3_qn), .clk(d_ff_2_qn), .Q(out_4[2]), .Qn(d_ff_3_qn), .reset(R));  // open: preset
  D_Flip_Flop d_ff_4 (.D(d_ff_4_qn), .clk(d_ff_3_qn), .Q(out_4[3]), .Qn(d_ff_4_qn), .reset(R));  // open: preset
  D_Flip_Flop d_ff_5 (.D(d_ff_5_qn), .clk(d_ff_4_qn), .Q(out_4[4]), .Qn(d_ff_5_qn), .reset(R));  // open: preset
  D_Flip_Flop d_ff_6 (.D(d_ff_6_qn), .clk(d_ff_5_qn), .Q(out_4[5]), .Qn(d_ff_6_qn), .reset(R));  // open: preset
  D_Flip_Flop d_ff_7 (.D(d_ff_7_qn), .clk(d_ff_6_qn), .Q(out_4[6]), .Qn(d_ff_7_qn), .reset(R));  // open: preset
  D_Flip_Flop d_ff_8 (.D(d_ff_8_qn), .clk(d_ff_7_qn), .Q(out_4[7]), .Qn(d_ff_8_qn), .reset(R));  // open: preset
  // Probe on out_4
endmodule

module Counter2Divider (
  input  [7:0] COUNTER,
  output [3:0] SS2,
  output [3:0] SS1,
  output [3:0] SS0
);

  wire [7:0] divider_1_rem;
  wire [7:4] divider_1_out, divider_2_out, divider_2_rem;

  // Probe on {divider_1_out, SS2}
  Divider divider_1 (.a(COUNTER), .b(8'h64), .out({divider_1_out, SS2}), .rem(divider_1_rem));  // open: upper
  // Probe on {divider_2_out, SS1}
  Divider divider_2 (
    .a(divider_1_rem), .b(8'ha), .out({divider_2_out, SS1}), .rem({divider_2_rem, SS0}));  // open: upper
  // Probe on {divider_2_rem, SS0}
endmodule

module SS (
  input  [3:0] in_1,
  output A,
  output B,
  output C,
  output D,
  output E,
  output F,
  output G
);

  wire and_1_out, and_2_out, and_3_out, and_4_out, and_5_out, and_6_out, and_7_out, and_8_out, and_9_out,
       and_10_out, and_11_out, and_12_out, and_13_out, and_14_out, and_15_out, and_16_out, and_17_out,
       and_18_out, and_19_out, and_20_out, and_21_out, and_22_out, and_23_out, and_24_out, and_25_out,
       and_26_out;

  and and_1 (and_1_out, ~in_1[3], ~in_1[2], in_1[1]);  // AND_Gate
  and and_2 (and_2_out, ~in_1[3], in_1[2], ~in_1[1]);  // AND_Gate
  and and_3 (and_3_out, ~in_1[3], in_1[2], ~in_1[0]);  // AND_Gate
  and and_4 (and_4_out, in_1[3], ~in_1[2], ~in_1[1]);  // AND_Gate
  and and_5 (and_5_out, ~in_1[3], in_1[2], ~in_1[1], in_1[0]);  // AND_Gate
  and and_6 (and_6_out, ~in_1[3], ~in_1[2], ~in_1[0]);  // AND_Gate
  and and_7 (and_7_out, ~in_1[3], ~in_1[2], in_1[1]);  // AND_Gate
  and and_8 (and_8_out, ~in_1[3], in_1[1], ~in_1[0]);  // AND_Gate
  and and_9 (and_9_out, in_1[3], ~in_1[2], ~in_1[1]);  // AND_Gate
  and and_10 (and_10_out, ~in_1[2], ~in_1[1], ~in_1[0]);  // AND_Gate
  and and_11 (and_11_out, ~in_1[3], in_1[1], ~in_1[0]);  // AND_Gate
  and and_12 (and_12_out, ~in_1[3], ~in_1[1], ~in_1[0]);  // AND_Gate
  and and_13 (and_13_out, ~in_1[3], in_1[2], ~in_1[1]);  // AND_Gate
  and and_14 (and_14_out, ~in_1[3], in_1[2], ~in_1[0]);  // AND_Gate
  and and_15 (and_15_out, in_1[3], ~in_1[2], ~in_1[1]);  // AND_Gate
  and and_16 (and_16_out, ~in_1[0], ~in_1[2], ~in_1[3]);  // AND_Gate
  and and_17 (and_17_out, ~in_1[3], in_1[2], in_1[0]);  // AND_Gate
  and and_18 (and_18_out, in_1[3], ~in_1[2], ~in_1[1]);  // AND_Gate
  and and_19 (and_19_out, in_1[1], ~in_1[3]);  // AND_Gate
  and and_20 (and_20_out, ~in_1[3], in_1[1], in_1[0]);  // AND_Gate
  and and_21 (and_21_out, ~in_1[3], ~in_1[1], ~in_1[0]);  // AND_Gate
  and and_22 (and_22_out, ~in_1[3], ~in_1[2]);  // AND_Gate
  and and_23 (and_23_out, ~in_1[2], ~in_1[1]);  // AND_Gate
  and and_24 (and_24_out, ~in_1[2], ~in_1[1]);  // AND_Gate
  and and_25 (and_25_out, ~in_1[3], in_1[0]);  // AND_Gate
  and and_26 (and_26_out, ~in_1[3], in_1[2]);  // AND_Gate
  or or_1 (E, and_10_out, and_11_out);
  or or_2 (F, and_12_out, and_13_out, and_14_out, and_15_out);
  or or_3 (G, and_1_out, and_2_out, and_3_out, and_4_out);
  or or_4 (C, and_24_out, and_25_out, and_26_out);
  or or_5 (D, and_5_out, and_6_out, and_7_out, and_8_out, and_9_out);
  or or_6 (A, and_16_out, and_17_out, and_18_out, and_19_out);
  or or_7 (B, and_20_out, and_21_out, and_22_out, and_23_out);
endmodule

module OCPLUSC2D (
  input  S1,
  input  S2,
  input  S3,
  input  CLK,
  input  R,
  output [3:0] S1SS2,
  output [3:0] S1SS1,
  output [3:0] S1SS0,
  output [3:0] S2SS2,
  output [3:0] S2SS1,
  output [3:0] S2SS0,
  output [3:0] S3SS2,
  output [3:0] S3SS1,
  output [3:0] S3SS0
);

  wire [7:0] ourcounter_1_out_4, ourcounter_2_out_4, ourcounter_3_out_4;

  OurCounter ourcounter_1 (.S(S1), .CLK(CLK), .R(R), .out_4(ourcounter_1_out_4));
  OurCounter ourcounter_2 (.S(S2), .CLK(CLK), .R(R), .out_4(ourcounter_2_out_4));
  OurCounter ourcounter_3 (.S(S3), .CLK(CLK), .R(R), .out_4(ourcounter_3_out_4));
  Counter2Divider counter2divider_1 (.COUNTER(ourcounter_1_out_4), .SS2(S1SS2), .SS1(S1SS1), .SS0(S1SS0));
  Counter2Divider counter2divider_2 (.COUNTER(ourcounter_2_out_4), .SS2(S2SS2), .SS1(S2SS1), .SS0(S2SS0));
  Counter2Divider counter2divider_3 (.COUNTER(ourcounter_3_out_4), .SS2(S3SS2), .SS1(S3SS1), .SS0(S3SS0));
endmodule
