// Logisim project MonocicloFINAL.circ as structural Verilog: 10 circuits, main circuit main
module main (
);

  wire alu_1_zero, alucntrl_1_jr, AluSRC, and_1_out, and_2_out, Branch, clock_1_out, controlunity_1_jal,
       controlunity_1_out_12, controlunity_1_regwrite, JUMP, MemRead, MemToReg, MemWrite, RegDist;
  wire [1:0] AluOP;
  wire [2:0] alucntrl_1_out_5;
  wire [3:0] adder_1_out;
  wire [4:0] divisor_1_rd, divisor_1_rs, divisor_1_rt, multiplexer_1_out;
  wire [5:0] divisor_1_function, divisor_1_opcode;
  wire [15:0] divisor_1_inmmediate;
  wire [25:0] divisor_1_address;
  wire [27:0] adder_1_out_2, shiftleft2_1_out;
  wire [31:0] _2PC, adder_2_out, address_memory_1_out_2, address_memory_1_out_3, alu_1_out_5,
       bit_extender_1_out, data_memory_1_readed_data, divider_1_out, multiplexer_2_out, multiplexer_3_out,
       multiplexer_4_out, multiplexer_5_out, multiplexer_6_out, PC_q, registers_1_rd1, registers_1_rd2,
       shifter_1_out;

  // Probe on divider_1_out
  Divider #(.width(32)) divider_1 (.a(PC_q), .b(32'h4), .out(divider_1_out));  // open: upper, rem
  Register #(.width(32)) PC (.D(_2PC), .Q(PC_q), .clk(clock_1_out));  // open: en, clr
  Address_Memory address_memory_1 (.in_1(PC_q), .out_2(address_memory_1_out_2), .out_3(address_memory_1_out_3));
  Clock clock_1 (.out(clock_1_out));
  ShiftLeft2 shiftleft2_1 (.address(divisor_1_address), .out(shiftleft2_1_out));
  Adder #(.width(32)) adder_1 (
    .a(address_memory_1_out_2), .b(32'h4), .out({adder_1_out, adder_1_out_2}));  // open: cin, cout
  Divisor divisor_1 (
    .in_1(address_memory_1_out_3), .FUNCTION(divisor_1_function), .INMMEDIATE(divisor_1_inmmediate),
    .RD(divisor_1_rd), .Address(divisor_1_address), .RT(divisor_1_rt), .RS(divisor_1_rs),
    .OpCode(divisor_1_opcode));  // open: SHAMT
  ControlUnity controlunity_1 (
    .Opcode(divisor_1_opcode), .RegDst(RegDist), .Jump(JUMP), .Branch(Branch), .MemRead(MemRead),
    .MemToReg(MemToReg), .AluOp(AluOP), .MemWrite(MemWrite), .AluSrc(AluSRC),
    .RegWrite(controlunity_1_regwrite), .out_12(controlunity_1_out_12), .JAL(controlunity_1_jal),
    .JR(alucntrl_1_jr));
  assign bit_extender_1_out = {{16{divisor_1_inmmediate[15]}}, divisor_1_inmmediate};  // Bit_Extender bit_extender_1
  Multiplexer #(.width(5), .enable("false")) multiplexer_1 (
    .in0(divisor_1_rt), .in1(divisor_1_rd), .out(multiplexer_1_out), .sel(RegDist));
  Registers registers_1 (
    .Write_Enable(controlunity_1_regwrite), .WR(multiplexer_1_out), .WD(multiplexer_6_out),
    .RD1(registers_1_rd1), .RD2(registers_1_rd2), .RR1(divisor_1_rs), .RR2(divisor_1_rt), .CLK(clock_1_out),
    .JAL(controlunity_1_jal), .in_2(alucntrl_1_jr));
  ALU alu_1 (
    .in_1(registers_1_rd1), .in_2(multiplexer_2_out), .in_3(alucntrl_1_out_5), .Zero(alu_1_zero),
    .out_5(alu_1_out_5));
  Multiplexer #(.width(32), .enable("false")) multiplexer_2 (
    .in0(registers_1_rd2), .in1(bit_extender_1_out), .out(multiplexer_2_out), .sel(AluSRC));
  ALUCntrl alucntrl_1 (
    .Function_OP(divisor_1_function), .in_2(controlunity_1_out_12), .AluOP(AluOP), .out_5(alucntrl_1_out_5),
    .JR(alucntrl_1_jr));
  Adder #(.width(32)) adder_2 (
    .a({adder_1_out, adder_1_out_2}), .b(shifter_1_out), .out(adder_2_out));  // open: cin, cout
  Shifter #(.width(32)) shifter_1 (.in(bit_extender_1_out), .\dist (5'b00010), .out(shifter_1_out));
  Multiplexer #(.width(32), .enable("false")) multiplexer_3 (
    .in0({adder_1_out, adder_1_out_2}), .in1(adder_2_out), .out(multiplexer_3_out), .sel(and_1_out));
  and and_1 (and_1_out, Branch, alu_1_zero);
  Data_Memory data_memory_1 (
    .Memory_Address(alu_1_out_5), .Data(registers_1_rd2), .MemWrite(MemWrite),
    .Readed_Data(data_memory_1_readed_data), .in_5(clock_1_out), .MemRead(MemRead));
  Multiplexer #(.width(32), .enable("false")) multiplexer_4 (
    .in0(multiplexer_3_out), .in1({adder_1_out, shiftleft2_1_out}), .out(multiplexer_4_out), .sel(JUMP));
  Multiplexer #(.width(32), .enable("false")) multiplexer_5 (
    .in0(alu_1_out_5), .in1(data_memory_1_readed_data), .out(multiplexer_5_out), .sel(MemToReg));
  Multiplexer #(.width(32), .enable("false")) multiplexer_6 (
    .in0(multiplexer_5_out), .in1({adder_1_out, adder_1_out_2}), .out(multiplexer_6_out),
    .sel(controlunity_1_jal));
  and and_2 (and_2_out, RegDist, alucntrl_1_jr);
  Multiplexer #(.width(32), .enable("false")) multiplexer_7 (
    .in0(multiplexer_4_out), .in1(registers_1_rd1), .out(_2PC), .sel(and_2_out));
endmodule

// IM
module Address_Memory (
  input  [31:0] in_1,
  output [31:0] out_2,
  output [31:0] out_3
);

  wire [31:0] shifter_1_out;

  Shifter #(.width(32), .shift("lr")) shifter_1 (.in(in_1), .\dist (5'b00010), .out(shifter_1_out));
  ROM #(.addrWidth(24), .dataWidth(32)) rom_1 (.addr(shifter_1_out[23:0]), .data(out_3), .sel(1'b1));

  assign out_2 = in_1;

  // Notes on the sheet:
  //   contents of rom_1 (hex, n*v repeats v):
  //   20100005 20080000 21290000 23180000 20042000 214a0000 8c8f0000 20112064 201220c8 22730001 1130000d
  //   1045820 8d6c0000 14c682a 18fc82a 11b30004 13330005 21080004 21290001 800000a 218a0000 8000011
  //   218f0000 8000011 ae2a0000 22310004 ae4f0000 22520004 23180001 13100004 20090000 200a0000 8d6f0004
  //   800000a
endmodule

// DM
module Data_Memory (
  input  [31:0] Memory_Address,
  input  [31:0] Data,
  input  MemRead,
  input  MemWrite,
  input  in_5,
  output [31:0] Readed_Data
);

  wire [23:0] subtractor_1_out;
  wire [31:0] shifter_1_out;

  Shifter #(.width(32), .shift("lr")) shifter_1 (.in(Memory_Address), .\dist (5'b00010), .out(shifter_1_out));
  Subtractor #(.width(24)) subtractor_1 (
    .a(shifter_1_out[23:0]), .b(24'h800), .out(subtractor_1_out));  // open: bin, bout
  RAM #(.addrWidth(24), .dataWidth(32), .bus("separate")) ram_1 (
    .addr(subtractor_1_out), .din(Data), .data(Readed_Data), .str(MemWrite), .clk(in_5), .ld(MemRead));  // open: sel, clr
endmodule

module Registers (
  input  CLK,
  input  in_2,
  input  [4:0] RR1,
  input  Write_Enable,
  input  [4:0] WR,
  input  JAL,
  input  [31:0] WD,
  input  [4:0] RR2,
  output [31:0] RD1,
  output [31:0] RD2
);

  wire decoder_1_out0, decoder_1_out1, decoder_1_out2, decoder_1_out3, decoder_1_out4, decoder_1_out5,
       decoder_1_out6, decoder_1_out7, decoder_1_out8, decoder_1_out9, decoder_1_out10, decoder_1_out11,
       decoder_1_out12, decoder_1_out13, decoder_1_out14, decoder_1_out15, decoder_1_out16, decoder_1_out17,
       decoder_1_out18, decoder_1_out19, decoder_1_out20, decoder_1_out21, decoder_1_out22, decoder_1_out23,
       decoder_1_out24, decoder_1_out25, decoder_1_out26, decoder_1_out27, decoder_1_out28, decoder_1_out29,
       decoder_1_out30, decoder_1_out31;
  wire [4:0] multiplexer_1_out, multiplexer_3_out;
  wire [31:0] register_1_q, register_2_q, register_3_q, register_4_q, register_5_q, register_6_q,
       register_7_q, register_8_q, register_9_q, register_10_q, register_11_q, register_12_q, register_13_q,
       register_14_q, register_15_q, register_16_q, register_17_q, register_18_q, register_19_q,
       register_20_q, register_21_q, register_22_q, register_23_q, register_24_q, register_25_q,
       register_26_q, S0_q, S1_q, S2_q, S3_q, t0_q, t1_q;

  Multiplexer #(.width(5), .enable("false")) multiplexer_1 (
    .in0(WR), .in1({5{1'b1}}), .out(multiplexer_1_out), .sel(JAL));
  Decoder #(.select(5), .disabled(0)) decoder_1 (
    .out0(decoder_1_out0), .out1(decoder_1_out1), .out2(decoder_1_out2), .out3(decoder_1_out3),
    .out4(decoder_1_out4), .out5(decoder_1_out5), .out6(decoder_1_out6), .out7(decoder_1_out7),
    .out8(decoder_1_out8), .out9(decoder_1_out9), .out10(decoder_1_out10), .out11(decoder_1_out11),
    .out12(decoder_1_out12), .out13(decoder_1_out13), .out14(decoder_1_out14), .out15(decoder_1_out15),
    .out16(decoder_1_out16), .out17(decoder_1_out17), .out18(decoder_1_out18), .out19(decoder_1_out19),
    .out20(decoder_1_out20), .out21(decoder_1_out21), .out22(decoder_1_out22), .out23(decoder_1_out23),
    .out24(decoder_1_out24), .out25(decoder_1_out25), .out26(decoder_1_out26), .out27(decoder_1_out27),
    .out28(decoder_1_out28), .out29(decoder_1_out29), .out30(decoder_1_out30), .out31(decoder_1_out31),
    .sel(multiplexer_1_out), .en(Write_Enable));
  // Probe on register_2_q
  Register #(.width(32)) register_1 (.en(decoder_1_out0), .Q(register_1_q), .clk(CLK));  // open: D, clr
  Register #(.width(32)) register_2 (.D(WD), .en(decoder_1_out4), .Q(register_2_q), .clk(CLK));  // open: clr
  Register #(.width(32)) t0 (.D(WD), .en(decoder_1_out8), .Q(t0_q), .clk(CLK));  // open: clr
  Register #(.width(32)) register_3 (.D(WD), .en(decoder_1_out12), .Q(register_3_q), .clk(CLK));  // open: clr
  Register #(.width(32)) S0 (.D(WD), .en(decoder_1_out16), .Q(S0_q), .clk(CLK));  // open: clr
  Register #(.width(32)) register_4 (.D(WD), .en(decoder_1_out20), .Q(register_4_q), .clk(CLK));  // open: clr
  Register #(.width(32)) register_5 (.D(WD), .en(decoder_1_out24), .Q(register_5_q), .clk(CLK));  // open: clr
  Register #(.width(32)) register_6 (.D(WD), .en(decoder_1_out28), .Q(register_6_q), .clk(CLK));  // open: clr
  Register #(.width(32)) register_7 (.D(WD), .en(decoder_1_out1), .Q(register_7_q), .clk(CLK));  // open: clr
  Register #(.width(32)) register_8 (.D(WD), .en(decoder_1_out5), .Q(register_8_q), .clk(CLK));  // open: clr
  Register #(.width(32)) t1 (.D(WD), .en(decoder_1_out9), .Q(t1_q), .clk(CLK));  // open: clr
  Register #(.width(32)) register_9 (.D(WD), .en(decoder_1_out13), .Q(register_9_q), .clk(CLK));  // open: clr
  Register #(.width(32)) S1 (.D(WD), .en(decoder_1_out17), .Q(S1_q), .clk(CLK));  // open: clr
  Register #(.width(32)) register_10 (.D(WD), .en(decoder_1_out21), .Q(register_10_q), .clk(CLK));  // open: clr
  Register #(.width(32)) register_11 (.D(WD), .en(decoder_1_out25), .Q(register_11_q), .clk(CLK));  // open: clr
  Register #(.width(32)) register_12 (.D(WD), .en(decoder_1_out29), .Q(register_12_q), .clk(CLK));  // open: clr
  Register #(.width(32)) register_13 (.D(WD), .en(decoder_1_out2), .Q(register_13_q), .clk(CLK));  // open: clr
  Register #(.width(32)) register_14 (.D(WD), .en(decoder_1_out6), .Q(register_14_q), .clk(CLK));  // open: clr
  Register #(.width(32)) register_15 (.D(WD), .en(decoder_1_out10), .Q(register_15_q), .clk(CLK));  // open: clr
  Register #(.width(32)) register_16 (.D(WD), .en(decoder_1_out14), .Q(register_16_q), .clk(CLK));  // open: clr
  Register #(.width(32)) S2 (.D(WD), .en(decoder_1_out18), .Q(S2_q), .clk(CLK));  // open: clr
  Register #(.width(32)) register_17 (.D(WD), .en(decoder_1_out22), .Q(register_17_q), .clk(CLK));  // open: clr
  Register #(.width(32)) register_18 (.D(WD), .en(decoder_1_out26), .Q(register_18_q), .clk(CLK));  // open: clr
  Register #(.width(32)) register_19 (.D(WD), .en(decoder_1_out30), .Q(register_19_q), .clk(CLK));  // open: clr
  Register #(.width(32)) register_20 (.D(WD), .en(decoder_1_out3), .Q(register_20_q), .clk(CLK));  // open: clr
  Register #(.width(32)) register_21 (.D(WD), .en(decoder_1_out7), .Q(register_21_q), .clk(CLK));  // open: clr
  Register #(.width(32)) register_22 (.D(WD), .en(decoder_1_out11), .Q(register_22_q), .clk(CLK));  // open: clr
  Register #(.width(32)) register_23 (.D(WD), .en(decoder_1_out15), .Q(register_23_q), .clk(CLK));  // open: clr
  // Probe on register_23_q
  Register #(.width(32)) S3 (.D(WD), .en(decoder_1_out19), .Q(S3_q), .clk(CLK));  // open: clr
  Register #(.width(32)) register_24 (.D(WD), .en(decoder_1_out23), .Q(register_24_q), .clk(CLK));  // open: clr
  Register #(.width(32)) register_25 (.D(WD), .en(decoder_1_out27), .Q(register_25_q), .clk(CLK));  // open: clr
  Register #(.width(32)) register_26 (.D(WD), .en(decoder_1_out31), .Q(register_26_q), .clk(CLK));  // open: clr
  Multiplexer #(.select(5), .width(32), .disabled(0), .enable("false")) multiplexer_2 (
    .in0(register_1_q), .in1(register_7_q), .in2(register_13_q), .in3(register_20_q), .in4(register_2_q),
    .in5(register_8_q), .in6(register_14_q), .in7(register_21_q), .in8(t0_q), .in9(t1_q),
    .in10(register_15_q), .in11(register_22_q), .in12(register_3_q), .in13(register_9_q),
    .in14(register_16_q), .in15(register_23_q), .in16(S0_q), .in17(S1_q), .in18(S2_q), .in19(S3_q),
    .in20(register_4_q), .in21(register_10_q), .in22(register_17_q), .in23(register_24_q),
    .in24(register_5_q), .in25(register_11_q), .in26(register_25_q), .in27(register_18_q),
    .in28(register_6_q), .in29(register_12_q), .in30(register_19_q), .in31(register_26_q), .out(RD1),
    .sel(multiplexer_3_out));
  Multiplexer #(.width(5), .enable("false")) multiplexer_3 (
    .in0(RR1), .in1({5{1'b1}}), .out(multiplexer_3_out), .sel(in_2));
  Multiplexer #(.select(5), .width(32), .disabled(0), .enable("false")) multiplexer_4 (
    .in0(register_1_q), .in1(register_7_q), .in2(register_13_q), .in3(register_20_q), .in4(register_2_q),
    .in5(register_8_q), .in6(register_14_q), .in7(register_21_q), .in8(t0_q), .in9(t1_q),
    .in10(register_15_q), .in11(register_22_q), .in12(register_3_q), .in13(register_9_q),
    .in14(register_16_q), .in15(register_23_q), .in16(S0_q), .in17(S1_q), .in18(S2_q), .in19(S3_q),
    .in20(register_4_q), .in21(register_10_q), .in22(register_17_q), .in23(register_24_q),
    .in24(register_5_q), .in25(register_11_q), .in26(register_25_q), .in27(register_18_q),
    .in28(register_6_q), .in29(register_12_q), .in30(register_19_q), .in31(register_26_q), .out(RD2),
    .sel(RR2));
endmodule

module ControlUnity (
  input  [5:0] Opcode,
  input  JR,
  output RegDst,
  output Jump,
  output Branch,
  output MemRead,
  output MemToReg,
  output [1:0] AluOp,
  output MemWrite,
  output AluSrc,
  output RegWrite,
  output out_12,
  output JAL
);

  wire [10:0] rom_1_data;

  and and_1 (out_12, ~Opcode[5], ~Opcode[4], ~Opcode[3], ~Opcode[2], ~Opcode[1], ~Opcode[0]);  // AND_Gate
  ROM #(.addrWidth(6), .dataWidth(11)) rom_1 (.addr(Opcode), .data(rom_1_data), .sel(1'b1));
  Multiplexer #(.width(11), .enable("false")) multiplexer_1 (
    .in0(rom_1_data), .in1({11{1'b0}}),
    .out({JAL, RegWrite, AluSrc, MemWrite, AluOp, MemToReg, MemRead, Branch, Jump, RegDst}), .sel(JR));

  // Notes on the sheet:
  //   contents of rom_1 (hex, n*v repeats v):
  //   241 0 2 2 24 0 0 0 300 26*0 318 7*0 180
endmodule

module ALUCntrl (
  input  [5:0] Function_OP,
  input  in_2,
  input  [1:0] AluOP,
  output JR,
  output [2:0] out_5
);

  wire [2:0] rom_1_data;

  and and_1 (JR, ~Function_OP[5], ~Function_OP[4], Function_OP[3], in_2, ~Function_OP[2], ~Function_OP[1], ~Function_OP[0]);  // AND_Gate
  ROM #(.addrWidth(6), .dataWidth(3)) rom_1 (.addr(Function_OP), .data(rom_1_data));  // open: sel
  Multiplexer #(.select(2), .width(3)) multiplexer_1 (
    .in0(3'b101), .in2(rom_1_data), .out(out_5), .sel(AluOP));  // open: in1, in3, en

  // Notes on the sheet:
  //   LW/SW
  //   contents of rom_1 (hex, n*v repeats v):
  //   8*0 7 23*0 5 0 6 0 3 1 4*0 4
endmodule

module ALU (
  input  [31:0] in_1,
  input  [31:0] in_2,
  input  [2:0] in_3,
  output Zero,
  output [31:0] out_5
);

  wire comparator_1_lt;
  wire [31:0] adder_1_out, and_1_out, bit_extender_1_out, nor_1_out, or_1_out, subtractor_1_out;

  Comparator #(.width(32)) comparator_1 (.a(in_1), .b(in_2), .eq(Zero), .lt(comparator_1_lt));  // open: gt
  Adder #(.width(32)) adder_1 (.a(in_1), .b(in_2), .out(adder_1_out));  // open: cin, cout
  Subtractor #(.width(32)) subtractor_1 (.a(in_1), .b(in_2), .out(subtractor_1_out));  // open: bin, bout
  assign bit_extender_1_out = {{31{1'b0}}, comparator_1_lt};  // Bit_Extender bit_extender_1
  assign and_1_out = in_1 & in_2;  // AND_Gate and_1, 32 bits wide
  assign or_1_out = in_1 | in_2;  // OR_Gate or_1, 32 bits wide
  assign nor_1_out = ~(in_1 | in_2);  // NOR_Gate nor_1, 32 bits wide
  Multiplexer #(.select(3), .width(32), .enable("false")) multiplexer_1 (
    .in0(nor_1_out), .in1(or_1_out), .in3(and_1_out), .in4(bit_extender_1_out), .in5(adder_1_out),
    .in6(subtractor_1_out), .in7(in_1), .out(out_5), .sel(in_3));  // open: in2
endmodule

module Divisor (
  input  [31:0] in_1,
  output [5:0] FUNCTION,
  output [15:0] INMMEDIATE,
  output [4:0] SHAMT,
  output [4:0] RD,
  output [25:0] Address,
  output [4:0] RT,
  output [4:0] RS,
  output [5:0] OpCode
);


  assign Address = in_1[25:0];
  assign FUNCTION = in_1[5:0];
  assign INMMEDIATE = in_1[15:0];
  assign OpCode = in_1[31:26];
  assign RD = in_1[15:11];
  assign RS = in_1[25:21];
  assign RT = in_1[20:16];
  assign SHAMT = in_1[10:6];
endmodule

module ShiftLeft (
  input  [25:0] address,
  input  [3:0] in_2,
  output [31:0] out
);


  assign out = {in_2, 2'b00, address};
endmodule

// SL2
module ShiftLeft2 (
  input  [25:0] address,
  output [27:0] out
);


  assign out = {address, 2'b00};
endmodule
